// Logisim project adders.circ as structural Verilog: 2 circuits, main circuit HalfAdder
module HalfAdder (
  input  Input_1,
  input  Input_2,
  output Output_1,
  output Output_2
);

  and and_1 (Output_2, Input_1, Input_1);
  xor xor_1 (Output_1, Input_1, Input_2);
endmodule

// FullAdder
module FullAddder (
  input  Input_1,
  input  Input_2,
  input  Input_3,
  output Output_1,
  output Output_2
);

  wire and_1_out, and_2_out, xor_1_out;

  xor xor_1 (xor_1_out, Input_1, Input_2);
  and and_1 (and_1_out, Input_1, Input_2);
  xor xor_2 (Output_1, xor_1_out, Input_3);
  and and_2 (and_2_out, xor_1_out, Input_3);
  or or_1 (Output_2, and_2_out, and_1_out);
endmodule
